// Logisim project jaw280.circ as structural Verilog: 6 circuits, main circuit main
module main (
);

  wire alu_neg, alu_zero, clear, clk, clock_1_out, dec7, display_enable, fl_update, halt, inc7, MultSrc,
       neg_out, ram_enable, reg_en, zero_out;
  wire [1:0] ALUSrcB;
  wire [2:0] rd;
  wire [3:0] DataSrc, display_unit_1_digit_1, display_unit_1_digit_2, display_unit_1_digit_3,
       display_unit_1_digit_4;
  wire [7:0] imm, lui_data;
  wire [15:0] alu_high, alu_inB, alu_out, data_in, mfhi_out, mflo_out, pc_out, ram_out, rom_out, rt_out,
       sxt_imm, zxt_imm;
  wire [15:8] rs_out;
  wire [31:0] bit_extender_3_out, mult_and_acc, prod_in;

  Clock clock_1 (.out(clock_1_out));
  and and_1 (clk, clock_1_out, ~halt);  // AND_Gate
  LED u_Halt (.in(halt));
  assign zxt_imm = {{8{1'b0}}, imm};  // Bit_Extender bit_extender_1
  assign sxt_imm = {{8{imm[7]}}, imm};  // Bit_Extender bit_extender_2
  Multiplexer #(.select(4), .width(16), .enable("false")) multiplexer_1 (
    .in0(zxt_imm), .in1({imm, lui_data}), .in2({rs_out, lui_data}), .in3(mfhi_out), .in4(mflo_out),
    .in5(ram_out), .in6(alu_out), .out(data_in), .sel(DataSrc));  // open: in7, in8, in9, in10, in11, in12, in13, in14, in15
  Hex_Digit_Display hex_digit_display_1 (.value(display_unit_1_digit_2));  // open: dp
  Hex_Digit_Display hex_digit_display_2 (.value(display_unit_1_digit_1));  // open: dp
  display_unit display_unit_1 (
    .Clock(clk), .Clear(clear), .Write_Enable(display_enable), .Data({rs_out, lui_data}),
    .Digit_1(display_unit_1_digit_1), .Digit_2(display_unit_1_digit_2), .Digit_3(display_unit_1_digit_3),
    .Digit_4(display_unit_1_digit_4));
  Hex_Digit_Display hex_digit_display_3 (.value(display_unit_1_digit_3));  // open: dp
  Hex_Digit_Display hex_digit_display_4 (.value(display_unit_1_digit_4));  // open: dp
  ROM #(.addrWidth(16), .dataWidth(16)) rom_1 (.addr(pc_out), .data(rom_out));  // open: sel
  RAM #(.addrWidth(16), .dataWidth(16), .bus("separate")) ram_1 (
    .addr({rs_out, lui_data}), .din(rt_out), .data(ram_out), .str(ram_enable), .clk(clk));  // open: sel, ld, clr
  Multiplexer #(.select(2), .width(16), .enable("false")) multiplexer_2 (
    .in0(rt_out), .in1(sxt_imm), .in2(zxt_imm), .out(alu_inB), .sel(ALUSrcB));  // open: in3
  Multiplexer #(.width(32), .enable("false")) multiplexer_3 (
    .in1(mult_and_acc), .out(prod_in), .sel(MultSrc));  // open: in0
  assign bit_extender_3_out = {{16{1'b0}}, alu_out};  // Bit_Extender bit_extender_3
  alu alu_1 (
    .A({rs_out, lui_data}), .B(alu_inB), .Result(alu_out), .High(alu_high), .Zero(alu_zero),
    .Negative(alu_neg));  // open: Operation
  program_counter_control program_counter_control_1 (
    .clock(clk), .Halt(halt), .Immediate(imm), .zero(zero_out), .negative(neg_out), .out_8(pc_out));  // open: opcode, rd_val
  Adder #(.width(32)) adder_1 (
    .a({mfhi_out, mflo_out}), .b(bit_extender_3_out), .out(mult_and_acc));  // open: cin, cout
  register_file register_file_1 (
    .Clock(clk), .Data(data_in), .Write_Enable(reg_en), .rd(rd), .incr7(inc7), .decr7(dec7),
    .rs_out({rs_out, lui_data}), .rt_out(rt_out));  // open: rs, rt, I_type
  // control control_1: pin names not known; wires that end beside it: rom_out, halt, display_enable, clear, imm, DataSrc, rd
  Register #(.width(1)) zero_register (.D(alu_zero), .en(fl_update), .Q(zero_out));  // open: clk, clr
  Register #(.width(1)) neg_register (.D(alu_neg), .en(fl_update), .Q(neg_out));  // open: clk, clr
  Register #(.width(32)) product_register (.D(prod_in), .Q({mfhi_out, mflo_out}));  // open: en, clk, clr

  // Other names for the same wires on the sheet: rs_out[7:0] = lui_data; lui_data[15:8] = imm;
  //   prod_out[31:0] = {mfhi_out, mflo_out}

  // Notes on the sheet:
  //   ROM
  //   RAM
endmodule

// display
module display_unit (
  input  Clock,
  input  Clear,
  input  Write_Enable,
  input  [15:0] Data,
  output [3:0] Digit_1,
  output [3:0] Digit_2,
  output [3:0] Digit_3,
  output [3:0] Digit_4
);

  Register #(.width(16)) register_1 (
    .D(Data), .en(Write_Enable), .Q({Digit_1, Digit_2, Digit_3, Digit_4}), .clk(Clock), .clr(Clear));

  // Other names for the same wires on the sheet: clk = Clock; clr = Clear
endmodule

module alu (
  input  [15:0] A,
  input  [15:0] B,
  input  [2:0] Operation,
  output [15:0] Result,
  output [15:0] High,
  output Zero,
  output Negative
);

  wire [15:0] add_out, and_out, left_out, mult_out, not_out, or_out, right_out, sub_out;

  Adder #(.width(16)) adder_1 (.a(A), .b(B), .out(add_out));  // open: cin, cout
  assign and_out = A & B;  // AND_Gate and_1, 16 bits wide
  Shifter #(.width(16)) shifter_1 (.in(A), .\dist (B[3:0]), .out(left_out));
  Subtractor #(.width(16)) subtractor_1 (.a(A), .b(B), .out(sub_out));  // open: bin, bout
  assign or_out = A | A;  // OR_Gate or_1, 16 bits wide
  Multiplexer #(.select(3), .width(16), .enable("false")) multiplexer_1 (
    .in0(add_out), .in1(sub_out), .in2(mult_out), .in3(and_out), .in4(or_out), .in5(not_out), .in6(left_out),
    .in7(right_out), .out(Result), .sel(Operation));
  Multiplier #(.width(16)) multiplier_1 (.a(A), .b(B), .out(mult_out), .cout(High));  // open: cin
  Shifter #(.width(16), .shift("lr")) shifter_2 (.in(A), .\dist (B[3:0]), .out(right_out));
  assign not_out = ~A;  // NOT_Gate not_1, 16 bits wide
  Comparator #(.width(16)) comparator_1 (.a(Result), .b({16{1'b0}}), .eq(Zero));  // open: gt, lt
  Comparator #(.width(16)) comparator_2 (.a(Result), .b({16{1'b0}}), .lt(Negative));  // open: gt, eq

  // Other names for the same wires on the sheet: mult_high[15:0] = High; op[2:0] = Operation

  // Notes on the sheet:
  //   000 - add
  //   011 - and
  //   110 - shift left
  //   001 - sub
  //   100 - or
  //   010 - mult
  //   111 - shift right
  //   101 - not
endmodule

module register_file (
  input  Clock,
  input  [15:0] Data,
  input  Write_Enable,
  input  [2:0] rd,
  input  [2:0] rs,
  input  [2:0] rt,
  input  incr7,
  input  decr7,
  input  I_type,
  output [15:0] rs_out,
  output [15:0] rt_out
);

  wire demultiplexer_1_out7, r0en, r1en, r2en, r3en, r4en, r5en, r6en, r7en;
  wire [2:0] multiplexer_1_out;
  wire [15:0] adder_1_out, r0out, r1out, r2out, r3out, r4out, r5out, r6out, r7input, r7input2, r7out, r7out1,
       subtractor_1_out, subtractor_2_out;

  Multiplexer #(.width(3), .enable("false")) multiplexer_1 (.in0(rs), .in1(rd), .out(multiplexer_1_out), .sel(I_type));
  Multiplexer #(.select(3), .width(16), .enable("false")) multiplexer_2 (
    .in0(r0out), .in1(r1out), .in2(r2out), .in3(r3out), .in4(r4out), .in5(r5out), .in6(r6out), .in7(r7out),
    .out(rs_out), .sel(multiplexer_1_out));
  Register #(.width(16)) r0 (.D(Data), .en(r0en), .Q(r0out), .clk(Clock));  // open: clr
  Register #(.width(16)) r4 (.D(Data), .en(r4en), .Q(r4out), .clk(Clock));  // open: clr
  Multiplexer #(.select(3), .width(16), .enable("false")) multiplexer_3 (
    .in0(r0out), .in1(r1out), .in2(r2out), .in3(r3out), .in4(r4out), .in5(r5out), .in6(r6out), .in7(r7out),
    .out(rt_out), .sel(rt));
  Subtractor #(.width(16)) subtractor_1 (.a(r7out1), .b(16'h1), .out(subtractor_1_out));  // open: bin, bout
  Register #(.width(16)) r1 (.D(Data), .en(r1en), .Q(r1out), .clk(Clock));  // open: clr
  Register #(.width(16)) r5 (.D(Data), .en(r5en), .Q(r5out), .clk(Clock));  // open: clr
  Adder #(.width(16)) adder_1 (.a(r7out1), .b(16'h1), .out(adder_1_out));  // open: cin, cout
  Subtractor #(.width(16)) subtractor_2 (.a(r7out1), .b(16'h1), .out(subtractor_2_out));  // open: bin, bout
  Multiplexer #(.width(16), .enable("false")) multiplexer_4 (
    .in0(r7out1), .in1(subtractor_1_out), .out(r7out), .sel(decr7));
  Register #(.width(16)) r2 (.D(Data), .en(r2en), .Q(r2out), .clk(Clock));  // open: clr
  Register #(.width(16)) r6 (.D(Data), .en(r6en), .Q(r6out), .clk(Clock));  // open: clr
  Demultiplexer #(.select(3), .enable("false")) demultiplexer_1 (
    .out0(r0en), .out1(r1en), .out2(r2en), .out3(r3en), .out4(r4en), .out5(r5en), .out6(r6en),
    .out7(demultiplexer_1_out7), .in(Write_Enable), .sel(rd));
  Multiplexer #(.width(16), .enable("false")) multiplexer_5 (.in0(Data), .in1(adder_1_out), .out(r7input), .sel(incr7));
  Multiplexer #(.width(16), .enable("false")) multiplexer_6 (
    .in0(r7input), .in1(subtractor_2_out), .out(r7input2), .sel(decr7));
  // Probe on r7input2
  Register #(.width(16)) r3 (.D(Data), .en(r3en), .Q(r3out), .clk(Clock));  // open: clr
  Register #(.width(16)) r7 (.D(r7input2), .en(r7en), .Q(r7out1), .clk(Clock));  // open: clr
  or or_1 (r7en, incr7, demultiplexer_1_out7, decr7);

  // Other names for the same wires on the sheet: CLK = Clock; ITYPE = I_type; RSOUT[15:0] = rs_out;
  //   RTOUT[15:0] = rt_out; WRE = Write_Enable
endmodule

// pc
module program_counter_control (
  input  clock,
  input  Halt,
  input  [7:0] Immediate,
  input  zero,
  input  negative,
  input  [6:0] opcode,
  input  [15:0] rd_val,
  output [15:0] out_8
);

  wire b, b_out, beq, beq_out, bez, bez_out, bge, bge_out, blt, blt_out, bne, bne_out, bnz, bnz_out, call,
       halt_t, i_type, pc_out_choose, rd_zero;
  wire [15:0] imm_sxt, pc__1, pc__1_off, pc_in;

  Adder #(.width(16)) adder_1 (.a(out_8), .b(16'h1), .out(pc__1));  // open: cin, cout
  assign imm_sxt = {{8{Immediate[7]}}, Immediate};  // Bit_Extender bit_extender_1
  Adder #(.width(16)) adder_2 (.a(pc__1), .b(imm_sxt), .out(pc__1_off));  // open: cin, cout
  not not_1 (halt_t, Halt);
  Comparator #(.width(16)) comparator_1 (.a(rd_val), .b({16{1'b0}}), .eq(rd_zero));  // open: gt, lt
  Demultiplexer #(.select(3), .enable("false")) demultiplexer_1 (
    .out0(b), .out1(blt), .out2(bge), .out3(beq), .out4(bne), .out5(bez), .out6(bnz), .out7(call),
    .in(i_type), .sel(opcode[2:0]));
  Comparator #(.width(2)) comparator_2 (.a(opcode[4:3]), .b(2'b11), .eq(i_type));  // open: gt, lt
  Register #(.width(16)) pc (.D(pc_in), .en(halt_t), .Q(out_8), .clk(clock));  // open: clr
  Multiplexer #(.width(16), .enable("false")) multiplexer_1 (
    .in0(pc__1), .in1(pc__1_off), .out(pc_in), .sel(pc_out_choose));
  Comparator #(.width(1)) comparator_3 (.a(b), .b(1'b1), .eq(b_out));  // open: gt, lt
  and and_1 (blt_out, blt, negative);
  and and_2 (bge_out, bge, ~negative);  // AND_Gate
  and and_3 (beq_out, beq, zero);
  and and_4 (bne_out, bne, ~zero);  // AND_Gate
  and and_5 (bez_out, bez, rd_zero);
  and and_6 (bnz_out, bnz, ~rd_zero);  // AND_Gate
  or or_1 (pc_out_choose, b_out, blt_out, bge_out, beq_out, bne_out, bez_out, bnz_out);

  // Other names for the same wires on the sheet: clk = clock; imm[7:0] = Immediate; neg = negative;
  //   code[2:0] = opcode[2:0]; type[1:0] = opcode[4:3]; pc_out[15:0] = out_8
endmodule

module control (
  input  [15:0] ROM_Input,
  output halt,
  output display_enable,
  output clear_display,
  output [7:0] imm,
  output [3:0] data_src,
  output [2:0] rd,
  output [2:0] rt,
  output [2:0] rs
);

  wire add, adi, \and , ani, b, beq, bez, bge, blt, bne, bnz, call, cmp, cpi, jr, ld, li, lui, mac, mfhi,
       mflo, mov, mul, \not , \or , ori, pop, push, r_type, ret, shl, shr, sli, sri, st, sub;

  Demultiplexer #(.select(5), .enable("false")) demultiplexer_1 (
    .out0(halt), .out1(display_enable), .out2(clear_display), .out3(mov), .out4(mfhi), .out5(mflo),
    .out6(ld), .out7(st), .out8(push), .out9(pop), .out10(add), .out11(sub), .out12(cmp), .out13(mul),
    .out14(mac), .out15(\and ), .out16(\or ), .out17(\not ), .out18(shl), .out19(shr), .out20(jr),
    .out21(ret), .in(r_type), .sel(ROM_Input[13:9]));  // open: out22, out23, out24, out25, out26, out27, out28, out29, out30, out31
  not not_1 (r_type, ROM_Input[15]);
  Demultiplexer #(.select(4), .enable("false")) demultiplexer_2 (
    .out0(li), .out1(lui), .out2(adi), .out3(ani), .out4(ori), .out5(sli), .out6(sri), .out7(cpi), .out8(b),
    .out9(blt), .out10(bge), .out11(beq), .out12(bne), .out13(bez), .out14(bnz), .out15(call),
    .in(ROM_Input[15]), .sel(ROM_Input[14:11]));
  Priority_Encoder #(.select(4)) priority_encoder_1 (
    .in0(1'b1), .in1(li), .in2(lui), .in3(mov), .in4(mfhi), .in5(mflo), .in6(ld), .out(data_src));  // open: in7, in8, in9, in10, in11, in12, in13, in14, in15, gs, en_out, en_in

  assign imm = ROM_Input[10:3];
  assign rd = ROM_Input[2:0];
  assign rs = ROM_Input[8:6];
  assign rt = ROM_Input[5:3];

  // Other names for the same wires on the sheet: clr = clear_display; put = display_enable;
  //   opcode_r[5:0] = ROM_Input[14:9]; opcode_i[3:0] = ROM_Input[14:11]; i_type = ROM_Input[15]

  // Notes on the sheet:
  //   r-type
  //   i-type
endmodule
